// Logisim project ttt_wkt.circ as structural Verilog: 1 circuit, main circuit main
module main (
);

  wire b1, b2, b3, b4, b5, b6, b7, b8, b9, clock_1_out, clock_2_out, clock_3_out, p1, p2, p3, p4, p5, p6, p7,
       p8, p9, Reset, Tie, Win;
  wire [3:0] register_1_q, rom_1_data, Xstate;
  wire [8:0] demultiplexer_1_out1, Omoves;

  Clock clock_1 (.out(clock_1_out));
  Clock clock_2 (.out(clock_2_out));
  // Probe on Omoves
  Register #(.width(4)) register_1 (.D(Xstate), .Q(register_1_q), .clk(clock_1_out), .clr(Reset));  // open: en
  J_K_Flip_Flop j_k_ff_1 (.J(p1), .clk(clock_2_out), .K(b1), .Q(Omoves[0]), .reset(Reset));  // open: Qn, preset, en
  J_K_Flip_Flop j_k_ff_2 (.J(p2), .clk(clock_2_out), .K(b2), .Q(Omoves[1]), .reset(Reset));  // open: Qn, preset, en
  J_K_Flip_Flop j_k_ff_3 (.J(p3), .clk(clock_2_out), .K(b3), .Q(Omoves[2]), .reset(Reset));  // open: Qn, preset, en
  J_K_Flip_Flop j_k_ff_4 (.J(p4), .clk(clock_2_out), .K(b4), .Q(Omoves[3]), .reset(Reset));  // open: Qn, preset, en
  J_K_Flip_Flop j_k_ff_5 (.J(p5), .clk(clock_2_out), .K(b5), .Q(Omoves[4]), .reset(Reset));  // open: Qn, preset, en
  J_K_Flip_Flop j_k_ff_6 (.J(p6), .clk(clock_2_out), .K(b6), .Q(Omoves[5]), .reset(Reset));  // open: Qn, preset, en
  J_K_Flip_Flop j_k_ff_7 (.J(p7), .clk(clock_2_out), .K(b7), .Q(Omoves[6]), .reset(Reset));  // open: Qn, preset, en
  J_K_Flip_Flop j_k_ff_8 (.J(p8), .clk(clock_2_out), .K(b8), .Q(Omoves[7]), .reset(Reset));  // open: Qn, preset, en
  J_K_Flip_Flop j_k_ff_9 (.J(p9), .clk(clock_2_out), .K(b9), .Q(Omoves[8]), .reset(Reset));  // open: Qn, preset, en
  // Probe on {Xstate, rom_1_data}
  ROM #(.addrWidth(13)) rom_1 (.addr({register_1_q, Omoves}), .data({Xstate, rom_1_data}));  // open: sel
  Clock clock_3 (.out(clock_3_out));
  J_K_Flip_Flop j_k_ff_10 (
    .J(demultiplexer_1_out1[0]), .clk(clock_3_out), .K(1'b0), .Q(b1), .reset(Reset));  // open: Qn, preset, en
  J_K_Flip_Flop j_k_ff_11 (
    .J(demultiplexer_1_out1[1]), .clk(clock_3_out), .K(1'b0), .Q(b2), .reset(Reset));  // open: Qn, preset, en
  J_K_Flip_Flop j_k_ff_12 (
    .J(demultiplexer_1_out1[2]), .clk(clock_3_out), .K(1'b0), .Q(b3), .reset(Reset));  // open: Qn, preset, en
  J_K_Flip_Flop j_k_ff_13 (
    .J(demultiplexer_1_out1[3]), .clk(clock_3_out), .K(1'b0), .Q(b4), .reset(Reset));  // open: Qn, preset, en
  J_K_Flip_Flop j_k_ff_14 (
    .J(demultiplexer_1_out1[4]), .clk(clock_3_out), .K(1'b0), .Q(b5), .reset(Reset));  // open: Qn, preset, en
  J_K_Flip_Flop j_k_ff_15 (
    .J(demultiplexer_1_out1[5]), .clk(clock_3_out), .K(1'b0), .Q(b6), .reset(Reset));  // open: Qn, preset, en
  J_K_Flip_Flop j_k_ff_16 (
    .J(demultiplexer_1_out1[6]), .clk(clock_3_out), .K(1'b0), .Q(b7), .reset(Reset));  // open: Qn, preset, en
  J_K_Flip_Flop j_k_ff_17 (
    .J(demultiplexer_1_out1[7]), .clk(clock_3_out), .K(1'b0), .Q(b8), .reset(Reset));  // open: Qn, preset, en
  J_K_Flip_Flop j_k_ff_18 (
    .J(demultiplexer_1_out1[8]), .clk(clock_3_out), .K(1'b0), .Q(b9), .reset(Reset));  // open: Qn, preset, en
  Demultiplexer #(.select(4), .enable("false")) demultiplexer_1 (
    .out1(demultiplexer_1_out1[0]), .out2(demultiplexer_1_out1[1]), .out3(demultiplexer_1_out1[2]),
    .out4(demultiplexer_1_out1[3]), .out5(demultiplexer_1_out1[4]), .out6(demultiplexer_1_out1[5]),
    .out7(demultiplexer_1_out1[6]), .out8(demultiplexer_1_out1[7]), .out9(demultiplexer_1_out1[8]),
    .out14(Tie), .out15(Win), .in(1'b1), .sel(rom_1_data));  // open: out0, out10, out11, out12, out13
  Button button_1 (.out(p1));
  LED led_1 (.in(Omoves[0]));
  LED led_2 (.in(Omoves[3]));
  Button button_2 (.out(p4));
  Button button_3 (.out(p7));
  LED led_3 (.in(Omoves[6]));
  Button button_4 (.out(Reset));
  LED led_4 (.in(b1));
  Button button_5 (.out(p2));
  LED led_5 (.in(b4));
  Button button_6 (.out(p5));
  Button button_7 (.out(p8));
  LED led_6 (.in(b7));
  LED led_7 (.in(Omoves[1]));
  Button button_8 (.out(p3));
  LED led_8 (.in(b2));
  LED led_9 (.in(Omoves[4]));
  Button button_9 (.out(p6));
  LED led_10 (.in(b5));
  LED led_11 (.in(b8));
  Button button_10 (.out(p9));
  LED led_12 (.in(Omoves[7]));
  LED led_13 (.in(Tie));
  LED led_14 (.in(Omoves[2]));
  LED led_15 (.in(b3));
  LED led_16 (.in(Omoves[5]));
  LED led_17 (.in(b6));
  LED led_18 (.in(Omoves[8]));
  LED led_19 (.in(b9));
  LED led_20 (.in(Win));

  // Other names for the same wires on the sheet: u1 = Omoves[0]; u2 = Omoves[1]; u3 = Omoves[2]; u4 = Omoves[3];
  //   u5 = Omoves[4]; u6 = Omoves[5]; u7 = Omoves[6]; u8 = Omoves[7]; u9 = Omoves[8];
  //   Xmoves[8:0] = {b9, b8, b7, b6, b5, b4, b3, b2, b1}

  // Notes on the sheet:
  //   contents of rom_1 (hex, n*v repeats v):
  //   0 15 11 0 15 0 0 0 11 7*0 10 10 10 0 10 0 0 0 10 7*0 13 6*20 0 20 20 20 0 20 0 0 0 10 30 20 30 20 30
  //   30 0 20 6*30 0 15 15*0 10 9*0 40 0 0 0 40 0 20 20 20 40 20 40 40 0 20 0 40 0 40 40 40 0 30 40 30 40
  //   30 30 40 0 30 0 30 0 30 0 0 0 12 15*0 10 15*0 20 20 20 0 20 0 0 0 20 7*0 20 6*30 0 30 30 30 0 30 6*0
  //   40 0 40 40 0 0 0 40 0 40 40 0 0 0 40 0 0 0 40 0 0 40 40 0 0 40 40 0 0 20 6*40 0 40 40 40 0 40 40 0 0
  //   40 40 30 0 40 40 0 0 30 7*0 15 15*0 10 15*0 20 20 20 0 20 0 0 0 20 7*0 7*30 0 30 30 30 0 30 6*0 40 0
  //   40 40 0 0 0 40 0 40 40 40 0 0 0 40 0 0 0 40 0 40 0 40 0 40 0 40 0 20 40 40 40 4*0 40 40 40 5*0 30 30
  //   40 0 30 0 0 0 30 39*0 20 15*0 30 30 30 0 30 0 0 0 30 10*0 40 0 40 40 0 0 40 40 0 40 40 40 5*0 40 0 0
  //   0 40 0 0 0 40 4*0 40 40 5*0 40 7*0 40 18*0 23 0 22 21 0 0 27 25 0 25 5*0 28 0 27 0 0 0 26 8*0 24 27
  //   0 29 0 0 0 25 7*0 24 16*0 24 21 0 22 0 0 0 21 7*0 23 15*0 21 32*0 27 25 0 24 0 0 0 23 7*0 21 15*0 21
  //   31*0 29 64*0 22 21 0 26 0 0 0 23 7*0 23 15*0 21 31*0 28 63*0 27 138*0 37 0 32 39 7*0 37 0 0 0 38 0
  //   37 6*0 35 0 38 31 0 0 37 31 0 39 4*0 39 34 0 37 14*0 34 0 34 35 0 0 0 39 0 35 5*0 38 5*0 33 8*0 35
  //   35 0 38 0 0 0 31 7*0 32 18*0 33 0 34 35 0 0 33 35 0 39 4*0 39 0 0 34 0 0 0 33 8*0 37 35 0 31 0 0 0
  //   32 7*0 34 16*0 34 39 0 35 0 0 0 33 7*0 32 15*0 31 34*0 34 0 32 36 0 0 37 35 0 31 5*0 33 0 34 0 0 0
  //   32 8*0 33 37 5*0 31 7*0 32 16*0 36 31 0 32 0 0 0 33 7*0 32 15*0 38 32*0 37 31 0 34 0 0 0 33 7*0 32
  //   15*0 33 106*0 3f 0 3f 3f 7*0 3f 7*0 49 4*0 3f 0 3f 3f 0 0 3f 0 0 3f 48 49 0 0 0 3f 49 3f 0 44 12*0
  //   3f 6*0 3f 13*0 3f 0 43 6*0 3f 3f 48 3f 48 49 0 3f 0 49 0 48 0 0 0 3f 42 44 18*0 3f 0 0 0 3f 0 0 3f
  //   46 6*0 3f 44 0 0 3f 46 0 0 47 5*0 3f 47 3f 44 41 0 3f 43 47 0 45 0 0 0 3f 42 0 0 44 12*0 3f 3f 46 3f
  //   44 46 0 3f 0 49 0 45 0 0 0 3f 46 6*0 42 7*0 3f 44 49 0 41 0 0 0 43 7*0 41 21*0 3f 6*0 48 47 5*0 3f 0
  //   44 0 3f 0 43 0 47 5*0 3f 45 4*0 3f 43 45 5*0 3f 0 44 14*0 3f 0 46 3f 46 44 0 3f 0 43 0 48 0 0 0 3f 0
  //   44 5*0 42 7*0 3f 48 48 5*0 43 7*0 42 16*0 3f 0 46 3f 46 46 0 3f 43 43 0 41 0 0 0 3f 0 0 0 44 0 0 0
  //   43 7*0 3f 45 44 5*0 43 7*0 42 109*0 4f 14*0 4f 4f 7*0 4f 35*0 4f 10*0 4f 4f 0 0 0 4f 0 4f 6*0 4e
  //   41*0 4e 5*0 4f 0 0 4f 0 0 4f 4f 0 4f 4e 6*0 4f 4e 13*0 4f 0 4f 4f 0 0 0 4f 0 4f 4*0 4f 6*0 4f 9*0 4f
  //   4e 4f 4e 0 0 4f 7*0 4f 4e 27*0 4f 8*0 4f 7*0 4e 4*0 4f 5*0 4f 4f 7*0 4f 16*0 4f 0 4f 4f 5*0 4f 0 4e
  //   9*0 4f 0 4e 6*0 4f 0 4e 4*0 4f 0 4e 5*0 4f 0 4e 16*0 4f 0 4f 4f 0 0 4f 4f 0 0 4e 4e 5*0 4f 0 0 0 4f
  //   0 0 0 4e 4*0 4f 4f 5*0 4f 7*0 4f
  //   Reset Button
endmodule
